# Fritzing sketch main_board (saved by Fritzing 0.9.4)
circuit board: 25.5cm x 9cm
breadboards: 1

parts:
  XTAL1 = Crystal [frequency="16 Mhz" package=THT]
  C3 = Ceramic Capacitor [capacitance=22pF voltage=10V package="100 mil [THT, multilayer]"]
  C2 = Ceramic Capacitor [capacitance=22pF voltage=10V package="100 mil [THT, multilayer]"]
  R1 = Resistor [tolerance=±5% resistance=10k package=THT]
  C1 = Ceramic Capacitor [capacitance=100nF voltage=10V package="100 mil [THT, multilayer]"]
  TTL1 = male pin header, 8 pins [form="♂ (male)"]
  TTL2 = male pin header, 8 pins [form="♂ (male)"]
  TTL3 = male pin header, 3 pins [form="♂ (male)"]
  TTL4 = male pin header, 3 pins [form="♂ (male)"]
  RESET = Pushbutton [package="[THT]"]
  U9 = atmega328 [package=dip]
  COOLANT = female pin header, 2 pins [form="♀ (female)"]
  ESTOP = female pin header, 2 pins [form="♀ (female)"]
  START/RESUME = female pin header, 2 pins [form="♀ (female)"]
  HOLD = female pin header, 2 pins [form="♀ (female)"]
  X_AXIS = female pin header, 8 pins [form="♀ (female)"]
  Y_AXIS = female pin header, 8 pins [form="♀ (female)"]
  Z_AXIS = female pin header, 8 pins [form="♀ (female)"]
  PROBE = female pin header, 2 pins [form="♀ (female)"]
  SPINDLE = female pin header, 4 pins [form="♀ (female)"]
  OUT1 = screw terminal, 2 pins
  OUT2 = screw terminal, 2 pins
  OUT3 = screw terminal, 2 pins
  FAN = female pin header, 2 pins [form="♀ (female)"]
  IN1 = screw terminal, 2 pins
  IN2 = screw terminal, 2 pins
  C4 = Electrolytic Capacitor [capacitance=100µF voltage=16V package="100 mil [THT, electrolytic]"]
  C5 = Ceramic Capacitor [capacitance=100nF voltage=10V package="100 mil [THT, multilayer]"]
  C6 = Ceramic Capacitor [capacitance=100nF package="100 mil [THT, multilayer]"]
  C7 = Ceramic Capacitor [capacitance=100nF package="100 mil [THT, multilayer]"]
  C8 = Ceramic Capacitor [capacitance=100nF package="100 mil [THT, multilayer]"]
  C9 = Ceramic Capacitor [capacitance=100nF package="100 mil [THT, multilayer]"]

nets:
  N1: XTAL1.pin_0, C3.1, U9.XLAT2
  N2: XTAL1.pin_1, C2.1, U9.XLAT1
  GND: C3.0, C2.0, TTL2.pin8, TTL4.pin1, RESET.Pin_3, RESET.Pin_4, U9.GND, COOLANT.pin2, ESTOP.pin2, START/RESUME.pin2, HOLD.pin2, X_AXIS.pin2, X_AXIS.pin4, X_AXIS.pin6, X_AXIS.pin8, Y_AXIS.pin2, Y_AXIS.pin4, Y_AXIS.pin6, Y_AXIS.pin8, Z_AXIS.pin2, Z_AXIS.pin4, Z_AXIS.pin6, Z_AXIS.pin8, PROBE.pin2, SPINDLE.pin2, SPINDLE.pin4, OUT1.pin1, OUT2.pin1, OUT3.pin1, FAN.pin2, IN1.pin1, IN2.pin1, C4.-, C5.0, C6.0, C7.0, C8.0, C9.0
  N3: R1.Pin_0, C1.1, RESET.Pin_1, RESET.Pin_2, U9.RESET
  5V: R1.Pin_1, TTL1.pin8, U9.VCC, U9.AVCC, U9.AREF, C4.+, C5.1
  N4: C1.0, TTL2.pin1
  N5: TTL3.pin1, TTL3.pin2
  N6: TTL4.pin2, U9.D1_(TX)
  N7: TTL4.pin3, U9.D0_(RX)
  N8: U9.D2, X_AXIS.pin1
  N9: U9.D3_(PWM), Y_AXIS.pin1
  N10: U9.D4, Z_AXIS.pin1
  N11: U9.D5_(PWM), X_AXIS.pin3
  N12: U9.D6_(PWM), Y_AXIS.pin3
  N13: U9.D7, Z_AXIS.pin3
  N14: U9.D8, X_AXIS.pin5, Y_AXIS.pin5, Z_AXIS.pin5
  N15: U9.D9_(PWM), X_AXIS.pin7, C7.1
  N16: U9.D10_(PWM), Y_AXIS.pin7, C8.1
  N17: U9.D11_(PWM), SPINDLE.pin1
  N18: U9.D12, Z_AXIS.pin7, C9.1
  N19: U9.D13, SPINDLE.pin3
  N20: U9.A0, ESTOP.pin1
  N21: U9.A1, HOLD.pin1
  N22: U9.A2, START/RESUME.pin1
  N23: U9.A3, COOLANT.pin1
  N24: U9.A5, PROBE.pin1, C6.1
  24V: OUT1.pin2, OUT2.pin2, OUT3.pin2, FAN.pin1, IN1.pin2, IN2.pin2
