# Fritzing sketch led (saved by Fritzing 0.9.3b)
circuit board: 3cm x 3cm
breadboards: 1

parts:
  LED1 = LED - 5mm [color="Red (633nm)" package="5 mm [THT]"]
  R1 = Resistor [tolerance=±5% resistance=220 package=THT]
  J1 = female pin header, 2 pins [form="♀ (female)"]

nets:
  GND: LED1.cathode, J1.pin2
  N1: LED1.anode, R1.Pin_1
  N2: R1.Pin_0, J1.pin1
